// Logisim project cpu_e2.circ as structural Verilog: 5 circuits, main circuit Test_cpu_here
module gpu (
  input  [7:0] addrs,
  input  write,
  input  [7:0] data,
  input  clk,
  input  print,
  output [3:0] x,
  output [3:0] y,
  output [7:0] c,
  output cd
);

  wire and_1_out, counter_1_carry, counter_2_carry, counter_4_q, not_1_out, or_1_out, t_ff_1_q, t_ff_1_qn;
  wire [7:0] controlled_buffer_1_out, controlled_buffer_3_out;

  assign controlled_buffer_1_out = write ? addrs : 8'bz;  // Controlled_Buffer controlled_buffer_1
  assign controlled_buffer_1_out = not_1_out ? {x, y} : 8'bz;  // Controlled_Buffer controlled_buffer_2
  not not_1 (not_1_out, write);
  RAM ram_1 (
    .addr(controlled_buffer_1_out), .we(write), .oe(t_ff_1_qn), .clk(clk), .din(controlled_buffer_3_out),
    .dout(c));
  Pull_Resistor pull_resistor_1 (.node(controlled_buffer_1_out));
  assign controlled_buffer_3_out = write ? data : 8'bz;  // Controlled_Buffer controlled_buffer_3
  Counter #(.max('hf), .width(4)) counter_1 (
    .Q(x), .carry(counter_1_carry), .clk(counter_2_carry), .clr(t_ff_1_q));  // open: load, D, count, up
  Counter #(.max('hf), .width(4)) counter_2 (
    .Q(y), .carry(counter_2_carry), .clk(clk), .clr(t_ff_1_q));  // open: load, D, count, up
  and and_1 (and_1_out, counter_4_q, clk);
  // RGB_Video #(.height(16), .scale(8), .width(16)) rgb_video_1: pin names not known; wires that end beside it: cd, clk, clk, c
  Counter #(.max('h1), .width(1)) counter_3 (
    .Q(cd), .clk(and_1_out), .clr(t_ff_1_qn));  // open: load, D, count, carry, up
  Counter #(.max('h1), .width(1)) counter_4 (
    .Q(counter_4_q), .clk(print), .clr(counter_4_q));  // open: load, D, count, carry, up
  T_Flip_Flop t_ff_1 (.T(or_1_out), .clk(or_1_out), .Q(t_ff_1_q), .Qn(t_ff_1_qn));  // open: reset, preset
  or or_1 (or_1_out, counter_1_carry, cd);
endmodule

module cpu_gpu (
  input  in_1,
  input  in_2,
  input  [1:0] in_3
);

  wire clock_1_out, not_1_out, rgb_video_1_p1;
  wire [3:0] rgb_video_1_p3, rgb_video_1_p4;
  wire [7:0] data_dout, inst_dout, pull_resistor_1_node, ram_1_dout, rgb_video_1_p5, v2_1_gcx, v2_1_gcy,
       v2_1_inst_req, v2_1_out2;

  RAM data (.addr(v2_1_inst_req), .oe(in_1), .clk(clock_1_out), .dout(data_dout));  // open: we, din
  RAM inst (.addr(v2_1_inst_req), .oe(in_1), .clk(clock_1_out), .dout(inst_dout));  // open: we, din
  Clock clock_1 (.out(clock_1_out));
  v2 v2_1 (
    .run(in_1), .inst(inst_dout), .clk(clock_1_out), .data(data_dout), .reset(in_2),
    .inst_REQ(v2_1_inst_req), .out2(v2_1_out2), .gcx(v2_1_gcx), .gcy(v2_1_gcy));  // open: in1, in2, in3, in4, RDI, sec_req, out1, out3, out4, RA, RDO, RW
  RAM #(.addrWidth(10)) ram_1 (
    .addr({in_3, v2_1_gcx}), .clk(clock_1_out), .din(pull_resistor_1_node), .dout(ram_1_dout));  // open: we, oe
  Pull_Resistor pull_resistor_1 (.node(pull_resistor_1_node));
  not not_1 (not_1_out, v2_1_out2[0]);
  // RGB_Video #(.height(16), .scale(8), .width(16)) rgb_video_1: pin names not known; wires that end beside it: rgb_video_1_p1, clock_1_out, rgb_video_1_p3, rgb_video_1_p4, rgb_video_1_p5
  gpu gpu_1 (
    .addrs(v2_1_gcy), .write(not_1_out), .data(ram_1_dout), .clk(clock_1_out), .print(v2_1_out2[0]),
    .x(rgb_video_1_p4), .y(rgb_video_1_p3), .c(rgb_video_1_p5), .cd(rgb_video_1_p1));
endmodule

module v2 (
  input  run,
  input  [7:0] inst,
  input  clk,
  input  [7:0] data,
  input  reset,
  input  [7:0] in1,
  input  [7:0] in2,
  input  [7:0] in3,
  input  [7:0] in4,
  input  [7:0] RDI,
  output [7:0] inst_REQ,
  output [7:0] sec_req,
  output [7:0] out1,
  output [7:0] out2,
  output [7:0] out3,
  output [7:0] out4,
  output [7:0] RA,
  output [7:0] RDO,
  output RW,
  output [7:0] gcx,
  output [7:0] gcy
);

  wire alu_1_jump, counter_2_carry, demultiplexer_1_out5, demultiplexer_1_out6, demultiplexer_1_out7,
       demultiplexer_1_out8, demultiplexer_1_out9, demultiplexer_1_out10, demultiplexer_1_out11,
       demultiplexer_1_out12, demultiplexer_1_out13, demultiplexer_1_out14, demultiplexer_1_out15,
       demultiplexer_1_out16, demultiplexer_1_out17, demultiplexer_1_out18, demultiplexer_1_out19,
       demultiplexer_1_out20, demultiplexer_1_out21, demultiplexer_1_out22, demultiplexer_1_out23,
       demultiplexer_1_out24, demultiplexer_1_out25, demultiplexer_1_out26, demultiplexer_1_out27,
       demultiplexer_1_out29, demultiplexer_1_out30, demultiplexer_1_out31, or_1_out, or_2_out, or_3_out,
       or_4_out, or_5_out, pull_resistor_1_node;
  wire [7:0] alu_1_out_alu, AR1_q, AR2_q, controlled_buffer_1_out, ZP_q, ZPE_q;

  or or_1 (or_1_out, demultiplexer_1_out23, alu_1_jump);
  assign controlled_buffer_1_out = demultiplexer_1_out27 ? data : 8'bz;  // Controlled_Buffer controlled_buffer_1
  Counter counter_1 (
    .load(or_1_out), .D(controlled_buffer_1_out), .Q(inst_REQ), .clk(counter_2_carry), .clr(reset));  // open: count, carry, up
  Counter #(.max('h1), .width(1)) counter_2 (.carry(counter_2_carry), .clk(clk));  // open: load, D, count, Q, up, clr
  Demultiplexer #(.select(5)) demultiplexer_1 (
    .out5(demultiplexer_1_out5), .out6(demultiplexer_1_out6), .out7(demultiplexer_1_out7),
    .out8(demultiplexer_1_out8), .out9(demultiplexer_1_out9), .out10(demultiplexer_1_out10),
    .out11(demultiplexer_1_out11), .out12(demultiplexer_1_out12), .out13(demultiplexer_1_out13),
    .out14(demultiplexer_1_out14), .out15(demultiplexer_1_out15), .out16(demultiplexer_1_out16),
    .out17(demultiplexer_1_out17), .out18(demultiplexer_1_out18), .out19(demultiplexer_1_out19),
    .out20(demultiplexer_1_out20), .out21(demultiplexer_1_out21), .out22(demultiplexer_1_out22),
    .out23(demultiplexer_1_out23), .out24(demultiplexer_1_out24), .out25(demultiplexer_1_out25),
    .out26(demultiplexer_1_out26), .out27(demultiplexer_1_out27), .out28(RW), .out29(demultiplexer_1_out29),
    .out30(demultiplexer_1_out30), .out31(demultiplexer_1_out31), .in(run), .sel(inst[4:0]));  // open: out0, out1, out2, out3, out4
  assign controlled_buffer_1_out = demultiplexer_1_out18 ? inst_REQ : 8'bz;  // Controlled_Buffer controlled_buffer_2
  or or_2 (or_2_out, demultiplexer_1_out31, demultiplexer_1_out30, RW, demultiplexer_1_out25, demultiplexer_1_out24, demultiplexer_1_out23, demultiplexer_1_out22, demultiplexer_1_out20, demultiplexer_1_out17, demultiplexer_1_out12, demultiplexer_1_out11, demultiplexer_1_out9, demultiplexer_1_out6);
  Register ZP (.D(controlled_buffer_1_out), .en(or_5_out), .clk(clk), .Q(ZP_q));  // open: clr
  or or_3 (or_3_out, demultiplexer_1_out9, demultiplexer_1_out10);
  or or_4 (or_4_out, demultiplexer_1_out6, demultiplexer_1_out7);
  assign controlled_buffer_1_out = or_2_out ? ZP_q : 8'bz;  // Controlled_Buffer controlled_buffer_3
  Register AR1 (.D(controlled_buffer_1_out), .en(demultiplexer_1_out30), .clk(clk), .Q(AR1_q));  // open: clr
  Register AR2 (.D(controlled_buffer_1_out), .en(demultiplexer_1_out31), .clk(clk), .Q(AR2_q));  // open: clr
  Register sr (.D(controlled_buffer_1_out), .en(demultiplexer_1_out17), .clk(clk), .Q(sec_req));  // open: clr
  Register o1 (.D(controlled_buffer_1_out), .en(demultiplexer_1_out24), .clk(clk), .Q(out1));  // open: clr
  assign controlled_buffer_1_out = demultiplexer_1_out21 ? in1 : 8'bz;  // Controlled_Buffer controlled_buffer_4
  assign controlled_buffer_1_out = demultiplexer_1_out15 ? in2 : 8'bz;  // Controlled_Buffer controlled_buffer_5
  Register o2 (.D(controlled_buffer_1_out), .en(demultiplexer_1_out22), .clk(clk), .Q(out2));  // open: clr
  assign controlled_buffer_1_out = demultiplexer_1_out14 ? in3 : 8'bz;  // Controlled_Buffer controlled_buffer_6
  assign controlled_buffer_1_out = demultiplexer_1_out13 ? in4 : 8'bz;  // Controlled_Buffer controlled_buffer_7
  Register o3 (.D(controlled_buffer_1_out), .en(demultiplexer_1_out12), .clk(clk), .Q(out3));  // open: clr
  Register o4 (.D(controlled_buffer_1_out), .en(demultiplexer_1_out11), .clk(clk), .Q(out4));  // open: clr
  Register RAM_ADDRESS (.D(controlled_buffer_1_out), .en(demultiplexer_1_out25), .clk(clk), .Q(RA));  // open: clr
  Register RAM_DATA (.D(controlled_buffer_1_out), .en(RW), .clk(clk), .Q(RDO));  // open: clr
  assign controlled_buffer_1_out = demultiplexer_1_out26 ? RDI : 8'bz;  // Controlled_Buffer controlled_buffer_8
  or or_5 (or_5_out, demultiplexer_1_out29, demultiplexer_1_out27, demultiplexer_1_out26, demultiplexer_1_out21, demultiplexer_1_out19, demultiplexer_1_out18, demultiplexer_1_out16, demultiplexer_1_out15, demultiplexer_1_out14, demultiplexer_1_out13, demultiplexer_1_out8, demultiplexer_1_out5, pull_resistor_1_node);
  assign controlled_buffer_1_out = demultiplexer_1_out8 ? gcx : 8'bz;  // Controlled_Buffer controlled_buffer_9
  Counter gc_x (
    .load(demultiplexer_1_out9), .D(controlled_buffer_1_out), .Q(gcx), .clk(or_3_out));  // open: count, carry, up, clr
  assign controlled_buffer_1_out = demultiplexer_1_out5 ? gcy : 8'bz;  // Controlled_Buffer controlled_buffer_10
  Counter gc_y (
    .load(demultiplexer_1_out6), .D(controlled_buffer_1_out), .Q(gcy), .clk(or_4_out));  // open: count, carry, up, clr
  Pull_Resistor pull_resistor_1 (.node(pull_resistor_1_node));
  assign controlled_buffer_1_out = demultiplexer_1_out16 ? sec_req : 8'bz;  // Controlled_Buffer controlled_buffer_11
  Register ZPE (.D(controlled_buffer_1_out), .en(demultiplexer_1_out20), .clk(clk), .Q(ZPE_q));  // open: clr
  assign controlled_buffer_1_out = demultiplexer_1_out19 ? ZPE_q : 8'bz;  // Controlled_Buffer controlled_buffer_12
  ALU alu_1 (
    .active(demultiplexer_1_out29), .opcode(inst[7:5]), .ar1(AR1_q), .ar2(AR2_q), .out_alu(alu_1_out_alu),
    .jump(alu_1_jump));
  assign controlled_buffer_1_out = demultiplexer_1_out29 ? alu_1_out_alu : 8'bz;  // Controlled_Buffer controlled_buffer_13
endmodule

module ALU (
  input  active,
  input  [2:0] opcode,
  input  [7:0] ar1,
  input  [7:0] ar2,
  output [7:0] out_alu,
  output jump
);

  wire comparator_1_eq, comparator_1_gt, comparator_1_lt, controlled_buffer_3_out, demultiplexer_1_out0,
       demultiplexer_1_out1, demultiplexer_1_out2, demultiplexer_1_out3, demultiplexer_1_out4,
       demultiplexer_1_out5, demultiplexer_1_out6, demultiplexer_1_out7, pull_resistor_2_node,
       pull_resistor_3_node;
  wire [7:0] adder_1_out, and_1_out, or_1_out, subtractor_1_out, xor_1_out;

  Demultiplexer #(.select(3)) demultiplexer_1 (
    .out0(demultiplexer_1_out0), .out1(demultiplexer_1_out1), .out2(demultiplexer_1_out2),
    .out3(demultiplexer_1_out3), .out4(demultiplexer_1_out4), .out5(demultiplexer_1_out5),
    .out6(demultiplexer_1_out6), .out7(demultiplexer_1_out7), .in(active), .sel(opcode));
  assign out_alu = demultiplexer_1_out0 ? adder_1_out : 8'bz;  // Controlled_Buffer controlled_buffer_1
  Adder adder_1 (.a(ar1), .b(ar2), .out(adder_1_out));  // open: cin, cout
  assign out_alu = demultiplexer_1_out2 ? subtractor_1_out : 8'bz;  // Controlled_Buffer controlled_buffer_2
  Subtractor subtractor_1 (.a(ar1), .b(ar2), .out(subtractor_1_out));  // open: bin, bout
  assign controlled_buffer_3_out = demultiplexer_1_out6 ? comparator_1_gt : 1'bz;  // Controlled_Buffer controlled_buffer_3
  Comparator comparator_1 (.a(ar1), .b(ar2), .gt(comparator_1_gt), .eq(comparator_1_eq), .lt(comparator_1_lt));
  assign and_1_out = ar1 & ar2;  // AND_Gate and_1, 8 bits wide
  assign out_alu = demultiplexer_1_out3 ? and_1_out : 8'bz;  // Controlled_Buffer controlled_buffer_4
  assign or_1_out = ar1 | ar2;  // OR_Gate or_1, 8 bits wide
  assign out_alu = demultiplexer_1_out4 ? or_1_out : 8'bz;  // Controlled_Buffer controlled_buffer_5
  assign xor_1_out = ar1 ^ ar2;  // XOR_Gate xor_1, 8 bits wide
  Pull_Resistor pull_resistor_1 (.node(controlled_buffer_3_out));
  Pull_Resistor pull_resistor_2 (.node(pull_resistor_2_node));
  assign pull_resistor_2_node = demultiplexer_1_out1 ? comparator_1_eq : 1'bz;  // Controlled_Buffer controlled_buffer_6
  Pull_Resistor pull_resistor_3 (.node(pull_resistor_3_node));
  assign pull_resistor_3_node = demultiplexer_1_out7 ? comparator_1_lt : 1'bz;  // Controlled_Buffer controlled_buffer_7
  assign out_alu = demultiplexer_1_out5 ? xor_1_out : 8'bz;  // Controlled_Buffer controlled_buffer_8
  or or_2 (jump, controlled_buffer_3_out, pull_resistor_2_node, pull_resistor_3_node);
  Pull_Resistor pull_resistor_4 (.node(out_alu));
endmodule

module Test_cpu_here (
  input  in_1,
  input  in_2,
  input  in_3
);

  wire clock_1_out, not_1_out, not_2_out, v2_1_rw;
  wire [3:0] v2_1_out2, v2_1_out3, v2_1_out3_2, v2_1_out4, v2_1_out4_2;
  wire [7:0] data_dout, inst_dout, ram_1_dout, v2_1_inst_req, v2_1_out1, v2_1_ra, v2_1_rdo, v2_1_sec_req;
  wire [7:4] v2_1_out2_2;

  Clock clock_1 (.out(clock_1_out));
  not not_1 (not_1_out, v2_1_rw);
  RAM #(.addrWidth(16)) inst (
    .addr({v2_1_sec_req, v2_1_inst_req}), .we(in_2), .oe(in_1), .clk(clock_1_out), .dout(inst_dout));  // open: din
  RAM #(.addrWidth(16)) data (
    .addr({v2_1_sec_req, v2_1_inst_req}), .we(in_2), .oe(in_1), .clk(clock_1_out), .dout(data_dout));  // open: din
  not not_2 (not_2_out, in_3);
  RAM ram_1 (.addr(v2_1_ra), .we(v2_1_rw), .oe(not_1_out), .clk(clock_1_out), .din(v2_1_rdo), .dout(ram_1_dout));
  v2 v2_1 (
    .run(in_3), .inst(inst_dout), .clk(clock_1_out), .data(data_dout), .reset(not_2_out), .RDI(ram_1_dout),
    .inst_REQ(v2_1_inst_req), .sec_req(v2_1_sec_req), .out1(v2_1_out1), .out2({v2_1_out2_2, v2_1_out2}),
    .out3({v2_1_out3_2, v2_1_out3}), .out4({v2_1_out4_2, v2_1_out4}), .RA(v2_1_ra), .RDO(v2_1_rdo),
    .RW(v2_1_rw));  // open: in1, in2, in3, in4, gcx, gcy
  Hex_Digit_Display hex_digit_display_1 (.value(v2_1_out1[7:4]));  // open: dp
  Hex_Digit_Display hex_digit_display_2 (.value(v2_1_out1[3:0]));  // open: dp
  Hex_Digit_Display hex_digit_display_3 (.value(v2_1_out2));  // open: dp
  Hex_Digit_Display hex_digit_display_4 (.value(v2_1_out2_2));  // open: dp
  Hex_Digit_Display hex_digit_display_5 (.value(v2_1_out3_2));  // open: dp
  Hex_Digit_Display hex_digit_display_6 (.value(v2_1_out3));  // open: dp
  Hex_Digit_Display hex_digit_display_7 (.value(v2_1_out4_2));  // open: dp
  Hex_Digit_Display hex_digit_display_8 (.value(v2_1_out4));  // open: dp
endmodule
